// Logisim project CircuitoS.circ as structural Verilog
module BOARD_BIG_ASM (
  output out_1
);

  wire button_1_out, CLK, CLR, d_ff_1_q, not_1_out, Write, Write_ASCII;
  wire [6:0] ASCII;
  wire [7:0] counter_1_q;
  wire [23:0] Dir_INPUT, Dir_MEMORY;
  wire [31:0] INPUT, MEMORY_IN, MEMORY_OUT;

  Button button_1 (.out(button_1_out));
  Clock clock_1 (.out(CLK));
  D_Flip_Flop d_ff_1 (.clk(CLK), .D(1'b1), .Q(d_ff_1_q), .reset(button_1_out));  // open: Qn, preset, en
  D_Flip_Flop d_ff_2 (.clk(CLK), .D(d_ff_1_q), .Qn(CLR), .reset(button_1_out));  // open: Q, preset, en
  BIG_ASM big_asm_1 (
    .DATA_INPUT(INPUT), .MEMORY_IN(MEMORY_OUT), .CLK(CLK), .CLR(CLR), .DIR_INPUT(Dir_INPUT),
    .MEMORY_OUT(MEMORY_IN), .DIR_MEMORY(Dir_MEMORY), .Write_OUTPUT(Write), .ASCII(ASCII),
    .Write_ASCII(Write_ASCII), .END(out_1));
  MEMORY memory_1 (.DIR(Dir_MEMORY), .DATA_IN(MEMORY_IN), .WRITE(Write), .CLK(CLK), .CLR(CLR), .DATA_OUT(MEMORY_OUT));
  INPUT input_1 (.DIR(Dir_INPUT), .CLK(CLK), .DATA_OUT(INPUT));
  Counter counter_1 (.load(1'b0), .count(not_1_out), .Q(counter_1_q), .clk(CLK), .clr(CLR));  // open: D, carry
  not not_1 (not_1_out, out_1);
  // Probe on counter_1_q
  TTY #(.rows(32), .cols(60)) tty_1 (.data(ASCII), .clk(CLK), .we(Write_ASCII), .clr(CLR));

  // Other names for the same wires on the sheet: END = out_1

  // Notes on the sheet:
  //   COUNTER
  //   BOARD
endmodule

module INPUT (
  input  [23:0] DIR,
  input  CLK,
  output [31:0] DATA_OUT
);

  RAM #(.addrWidth(24), .dataWidth(32)) ram_1 (.addr(DIR), .data(DATA_OUT), .clk(CLK), .ld(1'b1));  // open: sel, clr
endmodule

module MEMORY (
  input  [23:0] DIR,
  input  [31:0] DATA_IN,
  input  WRITE,
  input  CLK,
  input  CLR,
  output [31:0] DATA_OUT
);

  RAM #(.addrWidth(24), .dataWidth(32), .bus("separate")) ram_1 (
    .addr(DIR), .din(DATA_IN), .data(DATA_OUT), .str(WRITE), .clk(CLK), .clr(CLR));  // open: sel, ld
endmodule

module BIG_ASM (
  input  [31:0] DATA_INPUT,
  input  [31:0] MEMORY_IN,
  input  CLK,
  input  CLR,
  output [23:0] DIR_INPUT,
  output [31:0] MEMORY_OUT,
  output [23:0] DIR_MEMORY,
  output Write_OUTPUT,
  output [6:0] ASCII,
  output Write_ASCII,
  output END
);

  wire A____B, A___B, End_t, ENDD, LA, LAa, LB, LBb, LMCD, SA, SAs, SBs, Sn, start;
  wire [1:0] SB;
  wire [31:0] A, Aa, As, B, B_A, Bb, Bs;

  Starter starter_1 (.in_1(CLR), .in_2(CLK), .out_3(start));
  CONTROL_UNIT control_unit_1 (
    .A___B(A___B), .start(start), .Clock(CLK), .A____B(A____B), .CLR(CLR), .LA(LA), .SA(SA), .LAa(LAa),
    .SAs(SAs), .LMCD(LMCD), .wascll(Write_ASCII), .ascll(ASCII), .LB(LB), .SB(SB), .LBb(LBb), .SBs(SBs),
    .ENDD(ENDD), .End_2(End_t), .END(END), .Sn(Sn));
  DATA_PATH data_path_1 (
    .CLR(CLR), .LA(LA), .SA(SA), .LAa(LAa), .SAs(SAs), .LMCD(LMCD), .Input(DATA_INPUT), .N(DIR_INPUT),
    .LB(LB), .SB(SB), .LBb(LBb), .SBs(SBs), .Clock(CLK), .A___B(A___B), .Bs(Bs), .As(As), .A(A), .B(B),
    .Aa(Aa), .Bb(Bb), .B_A(B_A), .A____B(A____B), .Sn(Sn));

  // Other names for the same wires on the sheet: Clean = CLR; Clock = CLK; Input[31:0] = DATA_INPUT;
  //   N[23:0] = DIR_INPUT; WASCII = Write_ASCII
endmodule

module PRINT_UDEC (
  input  [31:0] num,
  input  start,
  input  CLK,
  input  RST,
  output [6:0] ASCII,
  output Write_ASCII,
  output \end 
);

  wire _0_c, _0_n, demultiplexer_1_out0, demultiplexer_2_out0, demultiplexer_2_out1, demultiplexer_3_out0,
       demultiplexer_3_out1, IDLE_2_q, IDLE_3_q, IDLE_4_q, IDLE_q, Lc, Lc_0, Ln, Ln_0, or_1_out;
  wire [23:0] bit_extender_1_out;
  wire [31:0] c, c___1, c___1_t, divider_1_rem, memory_1_data_out, multiplexer_1_out, multiplexer_2_out,
       multiplexer_3_out, n, n___10, n___10___48;

  Multiplexer #(.width(32), .enable("false")) multiplexer_1 (
    .in0(num), .in1(n___10), .out(multiplexer_1_out), .sel(Lc_0));
  Divider #(.width(32)) divider_1 (.a(n), .b(32'ha), .out(n___10), .rem(divider_1_rem));  // open: upper
  Adder #(.width(32)) adder_1 (.a(divider_1_rem), .b(32'h30), .out(n___10___48));  // open: cin, cout
  or or_1 (or_1_out, demultiplexer_1_out0, \end );
  Register #(.width(32)) u_n (.D(multiplexer_1_out), .en(Ln), .Q(n), .clk(CLK), .clr(RST));
  D_Flip_Flop IDLE (.clk(CLK), .D(or_1_out), .Q(IDLE_q), .preset(RST));  // open: Qn, en, reset
  Demultiplexer #(.enable("false")) demultiplexer_1 (
    .out0(demultiplexer_1_out0), .out1(Ln_0), .in(IDLE_q), .sel(start));
  or or_2 (Write_ASCII, demultiplexer_3_out0, demultiplexer_2_out1);
  Multiplexer #(.width(32), .enable("false")) multiplexer_2 (
    .in0(c___1), .in1(c___1_t), .out(multiplexer_2_out), .sel(Write_ASCII));
  Adder #(.width(32)) adder_2 (.a(c), .b(32'h1), .out(c___1));  // open: cin, cout
  Subtractor #(.width(32)) subtractor_1 (.a(c), .b(32'h1), .out(c___1_t));  // open: bin, bout
  D_Flip_Flop IDLE_2 (.clk(CLK), .D(Ln_0), .Q(IDLE_2_q), .reset(RST));  // open: Qn, preset, en
  Register #(.width(32)) u_c (.D(multiplexer_2_out), .en(Lc), .Q(c), .clk(CLK), .clr(RST));
  or or_3 (Lc_0, IDLE_2_q, demultiplexer_3_out1);
  Multiplexer #(.width(32), .enable("false")) multiplexer_3 (
    .in0(c), .in1(c___1_t), .out(multiplexer_3_out), .sel(Write_ASCII));
  Comparator #(.width(32), .mode("unsigned")) comparator_1 (.a({32{1'b0}}), .b(n), .lt(_0_n));  // open: gt, eq
  Comparator #(.width(32), .mode("unsigned")) comparator_2 (.a({32{1'b0}}), .b(c), .lt(_0_c));  // open: gt, eq
  D_Flip_Flop IDLE_3 (.clk(CLK), .D(Write_ASCII), .Q(IDLE_3_q), .reset(RST));  // open: Qn, preset, en
  Demultiplexer #(.enable("false")) demultiplexer_2 (
    .out0(demultiplexer_2_out0), .out1(demultiplexer_2_out1), .in(IDLE_3_q), .sel(_0_c));
  Bit_Extender #(.in_width(32), .out_width(24)) bit_extender_1 (.in(multiplexer_3_out), .out(bit_extender_1_out));
  D_Flip_Flop IDLE_4 (.clk(CLK), .D(Lc_0), .Q(IDLE_4_q), .reset(RST));  // open: Qn, preset, en
  or or_4 (Lc, Lc_0, Write_ASCII);
  or or_5 (Ln, Ln_0, Lc_0);
  Demultiplexer #(.enable("false")) demultiplexer_3 (
    .out0(demultiplexer_3_out0), .out1(demultiplexer_3_out1), .in(IDLE_4_q), .sel(_0_n));
  D_Flip_Flop IDLE_5 (.clk(CLK), .D(demultiplexer_2_out0), .Q(\end ), .reset(RST));  // open: Qn, preset, en
  MEMORY memory_1 (
    .DIR(bit_extender_1_out), .DATA_IN(n___10___48), .WRITE(Lc_0), .CLK(CLK), .CLR(RST),
    .DATA_OUT(memory_1_data_out));
  Bit_Extender #(.in_width(32), .out_width(7)) bit_extender_2 (.in(memory_1_data_out), .out(ASCII));

  // Other names for the same wires on the sheet: Lc_1 = Write_ASCII; Sc = Write_ASCII; Ln_1 = Lc_0; Sn = Lc_0;
  //   Write = Lc_0
endmodule

module PRINT_DEC (
  input  [31:0] num,
  input  start,
  input  CLK,
  input  RST,
  output [6:0] ASCII,
  output Write_ASCII,
  output END
);

  wire demultiplexer_1_out0, demultiplexer_1_out1, demultiplexer_2_out0, demultiplexer_3_out0, end_t,
       IDLE_3_q, IDLE_q, or_1_out, or_2_out, or_3_out, S_ASCII, startUDEC, Write_ASCII_1;
  wire [6:0] ASCII_t;
  wire [31:0] multiplexer_1_out, negator_1_out;

  or or_1 (or_1_out, demultiplexer_1_out0, END);
  Negator #(.width(32)) negator_1 (.in(num), .out(negator_1_out));
  D_Flip_Flop IDLE (.clk(CLK), .D(or_1_out), .Q(IDLE_q), .preset(RST));  // open: Qn, en, reset
  Demultiplexer #(.enable("false")) demultiplexer_1 (
    .out0(demultiplexer_1_out0), .out1(demultiplexer_1_out1), .in(IDLE_q), .sel(start));
  Multiplexer #(.width(32), .enable("false")) multiplexer_1 (
    .in0(num), .in1(negator_1_out), .out(multiplexer_1_out), .sel(num[31]));
  Demultiplexer #(.enable("false")) demultiplexer_2 (
    .out0(demultiplexer_2_out0), .out1(S_ASCII), .in(demultiplexer_1_out1), .sel(num[31]));
  or or_2 (or_2_out, demultiplexer_2_out0, S_ASCII);
  D_Flip_Flop IDLE_2 (.clk(CLK), .D(or_2_out), .Q(startUDEC), .reset(RST));  // open: Qn, preset, en
  PRINT_UDEC print_udec_1 (
    .num(multiplexer_1_out), .start(startUDEC), .CLK(CLK), .RST(RST), .ASCII(ASCII_t),
    .Write_ASCII(Write_ASCII_1), .\end (end_t));
  D_Flip_Flop IDLE_3 (.clk(CLK), .D(or_3_out), .Q(IDLE_3_q), .reset(RST));  // open: Qn, preset, en
  or or_3 (or_3_out, startUDEC, demultiplexer_3_out0);
  Demultiplexer #(.enable("false")) demultiplexer_3 (
    .out0(demultiplexer_3_out0), .out1(END), .in(IDLE_3_q), .sel(end_t));
  Multiplexer #(.width(7), .enable("false")) multiplexer_2 (
    .in0(ASCII_t), .in1(7'b0101101), .out(ASCII), .sel(S_ASCII));
  or or_4 (Write_ASCII, S_ASCII, Write_ASCII_1);

  // Other names for the same wires on the sheet: sign = num[31]; Write_ASCII_0 = S_ASCII
endmodule

module TEST_PRINT (
  input  [31:0] in_1,
  output out_2
);

  wire button_1_out, button_2_out, CLK, CLR, d_ff_1_q, Write_ASCII;
  wire [6:0] ASCII;

  Button button_1 (.out(button_1_out));
  Clock clock_1 (.out(CLK));
  D_Flip_Flop d_ff_1 (.clk(CLK), .D(1'b1), .Q(d_ff_1_q), .reset(button_1_out));  // open: Qn, preset, en
  D_Flip_Flop d_ff_2 (.clk(CLK), .D(d_ff_1_q), .Qn(CLR), .reset(button_1_out));  // open: Q, preset, en
  Button button_2 (.out(button_2_out));
  PRINT_UDEC print_udec_1 ();  // open: num, start, CLK, RST, ASCII, Write_ASCII, end
  PRINT_DEC print_dec_1 (
    .num(in_1), .start(button_2_out), .CLK(CLK), .RST(CLR), .ASCII(ASCII), .Write_ASCII(Write_ASCII),
    .END(out_2));
  TTY #(.rows(32), .cols(60)) tty_1 (.data(ASCII), .clk(CLK), .we(Write_ASCII), .clr(CLR));
endmodule

module DATA_PATH (
  input  CLR,
  input  LA,
  input  SA,
  input  LAa,
  input  SAs,
  input  LMCD,
  input  [31:0] Input,
  input  LB,
  input  [1:0] SB,
  input  LBb,
  input  SBs,
  input  Clock,
  input  Sn,
  output [23:0] N,
  output A___B,
  output [31:0] Bs,
  output [31:0] As,
  output [31:0] A,
  output [31:0] B,
  output [31:0] Aa,
  output [31:0] Bb,
  output [31:0] B_A,
  output A____B
);

  wire comparator_1_eq;
  wire [31:0] B___A, MCD, multiplexer_1_out, multiplexer_2_out, multiplexer_3_out, multiplexer_4_out;

  Multiplexer #(.width(32), .enable("false")) multiplexer_1 (.in0(Input), .in1(B), .out(multiplexer_1_out), .sel(SA));
  Multiplexer #(.width(32), .enable("false")) multiplexer_2 (.in0(Input), .in1(As), .out(multiplexer_2_out), .sel(SAs));
  Comparator #(.width(32)) comparator_1 (.a(A), .b(B), .gt(A___B), .eq(comparator_1_eq));  // open: lt
  Register #(.width(32)) R1 (.D(multiplexer_1_out), .en(LA), .Q(A), .clk(Clock), .clr(CLR));
  Register #(.width(32)) R3 (.D(multiplexer_2_out), .en(LAa), .Q(Aa), .clk(Clock), .clr(CLR));
  not not_1 (A____B, comparator_1_eq);
  Multiplexer #(.select(2), .width(32), .enable("false")) multiplexer_3 (
    .in0(Input), .in1(A), .in2(B___A), .out(multiplexer_3_out), .sel(SB));  // open: in3
  Subtractor #(.width(32)) subtractor_1 (.a(B), .b(A), .out(B___A));  // open: bin, bout
  Multiplexer #(.width(32), .enable("false")) multiplexer_4 (.in0(Input), .in1(Bs), .out(multiplexer_4_out), .sel(SBs));
  Register #(.width(32)) R2 (.D(multiplexer_3_out), .en(LB), .Q(B), .clk(Clock), .clr(CLR));
  Register #(.width(32)) R4 (.D(multiplexer_4_out), .en(LBb), .Q(Bb), .clk(Clock), .clr(CLR));
  Divider #(.width(32)) divider_1 (.a(Aa), .b(MCD), .out(As));  // open: upper, rem
  Register #(.width(32)) R5 (.D(A), .en(LMCD), .Q(MCD), .clk(Clock), .clr(CLR));
  Divider #(.width(32)) divider_2 (.a(Bb), .b(MCD), .out(Bs));  // open: upper, rem
  Multiplexer #(.width(24), .enable("false")) multiplexer_5 (.in0({24{1'b0}}), .in1(24'h1), .out(N), .sel(Sn));

  // Other names for the same wires on the sheet: Clean = CLR
endmodule

module CONTROL_UNIT (
  input  A___B,
  input  start,
  input  Clock,
  input  A____B,
  input  CLR,
  output END,
  output Sn,
  output LA,
  output SA,
  output LAa,
  output SAs,
  output LMCD,
  output wascll,
  output [6:0] ascll,
  output LB,
  output [1:0] SB,
  output LBb,
  output SBs,
  output ENDD,
  output End_2
);

  wire demultiplexer_1_out0, demultiplexer_2_out0, demultiplexer_2_out1, demultiplexer_3_out1,
       demultiplexer_4_out0, demultiplexer_5_out0, demultiplexer_5_out1, demultiplexer_6_out0,
       demultiplexer_6_out1, End_2_q, End_q, IDLE_q, LA0, LAa0, LBb0, or_1_out, or_5_out, or_6_out, or_9_out,
       or_10_out, or_11_out, wascii0, wascii_t, While_q;
  wire [6:0] ascii0, ascii_t;
  wire [31:0] Aa, Bb;

  or or_1 (or_1_out, demultiplexer_1_out0, demultiplexer_6_out1);
  or or_2 (LA, LA0, SA);
  or or_3 (LB, Sn, SA, SB[1]);
  or or_4 (wascll, wascii0, wascii_t);
  D_Flip_Flop IDLE (.clk(Clock), .D(or_1_out), .Q(IDLE_q), .preset(CLR));  // open: Qn, en, reset
  Demultiplexer #(.enable("false")) demultiplexer_1 (.out0(demultiplexer_1_out0), .out1(LA0), .in(IDLE_q), .sel(start));
  or or_5 (or_5_out, demultiplexer_2_out0, SAs);
  D_Flip_Flop d_ff_1 (.clk(Clock), .D(LA0), .Q(Sn), .reset(CLR));  // open: Qn, preset, en
  Multiplexer #(.width(7), .enable("false")) multiplexer_1 (.in0(ascii0), .in1(ascii_t), .out(ascll), .sel(wascii_t));
  D_Flip_Flop u_End (.clk(Clock), .D(or_5_out), .Q(End_q), .reset(CLR));  // open: Qn, preset, en
  Demultiplexer #(.enable("false")) demultiplexer_2 (
    .out0(demultiplexer_2_out0), .out1(demultiplexer_2_out1), .in(End_q), .sel(ENDD));
  or or_6 (or_6_out, Sn, SB[1]);
  D_Flip_Flop d_ff_2 (.clk(Clock), .D(LAa0), .Q(LBb0), .reset(CLR));  // open: Qn, preset, en
  Demultiplexer #(.enable("false")) demultiplexer_3 (
    .out0(LAa0), .out1(demultiplexer_3_out1), .in(While_q), .sel(A____B));
  D_Flip_Flop While (.clk(Clock), .D(or_6_out), .Q(While_q), .reset(CLR));  // open: Qn, preset, en
  or or_7 (LAa, LAa0, SAs);
  Demultiplexer #(.enable("false")) demultiplexer_4 (
    .out0(demultiplexer_4_out0), .out1(SA), .in(demultiplexer_3_out1), .sel(A___B));
  D_Flip_Flop d_ff_3 (.clk(Clock), .D(LBb0), .Q(LMCD), .preset(CLR), .en(CLR), .reset(CLR));  // open: Qn
  or or_8 (LBb, LBb0, SAs);
  or or_9 (or_9_out, demultiplexer_4_out0, SA);
  PRINT_UDEC Print_a_simp (
    .num(Aa), .start(SAs), .CLK(Clock), .RST(CLR), .ASCII(ascii0), .Write_ASCII(wascii0), .\end (ENDD));
  D_Flip_Flop d_ff_4 (.clk(Clock), .D(LMCD), .Q(SAs), .reset(CLR));  // open: Qn, preset, en
  D_Flip_Flop After_If (.clk(Clock), .D(or_9_out), .Q(SB[1]), .reset(CLR));  // open: Qn, preset, en
  or or_10 (or_10_out, demultiplexer_5_out0, demultiplexer_2_out1);
  PRINT_UDEC Print_b_simp (
    .num(Bb), .start(demultiplexer_2_out1), .CLK(Clock), .RST(CLR), .ASCII(ascii_t), .Write_ASCII(wascii_t),
    .\end (End_2));
  Demultiplexer #(.enable("false")) demultiplexer_5 (
    .out0(demultiplexer_5_out0), .out1(demultiplexer_5_out1), .in(End_2_q), .sel(End_2));
  D_Flip_Flop u_End_2 (.clk(Clock), .D(or_10_out), .Q(End_2_q), .reset(CLR));  // open: Qn, preset, en
  or or_11 (or_11_out, demultiplexer_6_out0, demultiplexer_5_out1);
  D_Flip_Flop End_3 (.clk(Clock), .D(or_11_out), .Q(END), .reset(CLR));  // open: Qn, preset, en
  Demultiplexer #(.enable("false")) demultiplexer_6 (
    .out0(demultiplexer_6_out0), .out1(demultiplexer_6_out1), .in(END), .sel(CLR));

  assign SB[0] = SA;
  assign SBs = SAs;

  // Other names for the same wires on the sheet: ASCII[6:0] = ascll; Clean = CLR; End_t = End_2; LB0 = Sn; LAa1 = SAs;
  //   LBb1 = SAs; LA1 = SA; LB1 = SA; SB0 = SA; LB2 = SB[1]; WASCII = wascll
endmodule

module Starter (
  input  in_1,
  input  in_2,
  output out_3
);

  wire En, not_1_out;

  not not_1 (not_1_out, in_1);
  D_Flip_Flop d_ff_1 (.clk(in_2), .D(1'b1), .Qn(En), .en(not_1_out), .reset(in_1));  // open: Q, preset
  and and_1 (out_3, ~in_1, En);  // AND_Gate

  // Other names for the same wires on the sheet: Clean = in_1; Clock = in_2
endmodule
